# Fritzing sketch 5V_3.3V_2.5V_PowerSupply_2 (saved by Fritzing 0.9.3b)
breadboards: 3

parts:
  U1 = Voltage Regulator - 5V [package="TO220 [THT]"]
  D1 = Rectifier Diode [part_number=1N4001 package="300 mil [THT]"]
  C1 = Ceramic Capacitor [capacitance=100nF package="100 mil [THT, multilayer]"]
  C2 = Ceramic Capacitor [capacitance=100nF package="100 mil [THT, multilayer]"]
  D2 = Rectifier Diode [part_number=1N4001 package="300 mil [THT]"]
  VCC1 = Battery block 9V
  F1 = Resettable Fuse PTC [package=ptc]
  D3 = Rectifier Diode [part_number=1N4001 package="300 mil [THT]"]
  R1 = Resistor [tolerance=±5% resistance=1k package=THT]
  LED1 = LED - 3mm [color="Orange (620nm)" package="3 mm [THT]"]
  U4 = Voltage Regulator - 5V [package="TO220 [THT]"]
  C8 = Ceramic Capacitor [capacitance=100nF package="100 mil [THT, multilayer]"]
  D7 = Rectifier Diode [part_number=1N4001 package="300 mil [THT]"]
  C10 = Electrolytic Capacitor [capacitance=1µF package="100 mil [THT, electrolytic]"]
  C11 = Ceramic Capacitor [capacitance=100nF package="100 mil [THT, multilayer]"]
  D8 = Rectifier Diode [part_number=1N4001 package="300 mil [THT]"]
  F2 = Resettable Fuse PTC [package=ptc]
  VCC2 = Battery block 9V
  LED2 = LED - 3mm [color="Blue (505nm)" package="3 mm [THT]"]
  R2 = Resistor [tolerance=±5% resistance=10k package=THT]
  LED3 = LED - 3mm [color="Red (633nm)" package="3 mm [THT]"]
  R3 = Resistor [tolerance=±5% resistance=1k package=THT]
  IC1 = Dual Op-Amp [package=dip08]
  R4 = Resistor [tolerance=±5% resistance=10k package=THT]
  R5 = Resistor [tolerance=±5% resistance=10k package=THT]
  C12 = Ceramic Capacitor [capacitance=100nF package="100 mil [THT, multilayer]"]
  C14 = Electrolytic Capacitor [capacitance=1µF package="100 mil [THT, electrolytic]"]
  C15 = Ceramic Capacitor [capacitance=100nF package="100 mil [THT, multilayer]"]
  C16 = Electrolytic Capacitor [capacitance=1µF package="100 mil [THT, electrolytic]"]
  LED4 = LED - 3mm [color="Green (565nm)" package="3 mm [THT]"]
  R6 = Resistor [tolerance=±5% resistance=10 package=THT]
  R7 = Resistor [tolerance=±5% resistance=220 package=THT]
  LED5 = LED - 3mm [color="Yellow (595nm)" package="3 mm [THT]"]

nets:
  N1: U1.input_voltage, D1.cathode, C1.1, D2.cathode
  GND: U1.GND, C1.0, C2.1, VCC1.-, D3.anode, R1.Pin_1, U4.GND, C8.0, C10.+, C11.1, D8.anode, VCC2.+, LED2.anode, R3.Pin_0, IC1.A_V-, IC1.B_+IN, R5.Pin_1, C15.0, C16.-, R6.Pin_1, R7.Pin_1
  N2: U1.output_voltage, D1.anode, C2.0, D3.cathode, LED1.anode, U4.input_voltage, C8.1, D7.cathode, C10.-, IC1.A_V+, R4.Pin_1, C12.1, C14.+
  N3: D2.anode, F1.2, LED3.anode
  N4: VCC1.+, F1.1
  N5: R1.Pin_0, LED1.cathode
  N6: U4.output_voltage, D7.anode, C11.0, D8.cathode, LED5.anode
  N7: F2.1, VCC2.-
  N8: F2.2, R2.Pin_0
  N9: LED2.cathode, R2.Pin_1
  N10: LED3.cathode, R3.Pin_1
  N11: IC1.A_OUT, IC1.A_-IN, C12.0, C14.-, C15.1, C16.+, LED4.anode
  N12: IC1.A_+IN, R4.Pin_0, R5.Pin_0
  N13: IC1.B_-IN, IC1.B_OUT
  N14: LED4.cathode, R6.Pin_0
  N15: R7.Pin_0, LED5.cathode

notes:
  GND
  +9V
  GND
  +5V
  +3.3V
  -9V
  GND
  +2.5V
