# Fritzing sketch BaseMachine UI Controller & Sequencer (saved by Fritzing 0.9.2b)
perfboards: 3
breadboards: 1

parts:
  J1 = STM32 Nucleo boards
  J3 = female pin header, 8 pins [form="♀ (female)"]
  J4 = female pin header, 6 pins [form="♀ (female)"]
  J2 = female pin header, 6 pins [form="♀ (female)"]
  J5 = female pin header, 5 pins [form="♀ (female)"]
  J6 = female pin header, 5 pins [form="♀ (female)"]
  J7 = female pin header, 5 pins [form="♀ (female)"]
  J8 = female pin header, 8 pins [form="♀ (female)"]
  J9 = female pin header, 2 pins [form="♀ (female)"]
  J10 = STM32 Nucleo boards
  LED1 = LED - 3mm [color="Red (633nm)" package="3 mm [THT]"]
  LED2 = LED - 3mm [color="Red (633nm)" package="3 mm [THT]"]
  LED3 = LED - 3mm [color="Red (633nm)" package="3 mm [THT]"]
  LED4 = LED - 3mm [color="Red (633nm)" package="3 mm [THT]"]
  LED5 = LED - 3mm [color="Red (633nm)" package="3 mm [THT]"]
  LED6 = LED - 3mm [color="Red (633nm)" package="3 mm [THT]"]
  R1 = Resistor [tolerance=±5% resistance=1k package=THT]
  R2 = Resistor [tolerance=±5% resistance=1k package=THT]
  R3 = Resistor [tolerance=±5% resistance=1k package=THT]
  R4 = Resistor [tolerance=±5% resistance=1k package=THT]
  R5 = Resistor [tolerance=±5% resistance=1k package=THT]
  R6 = Resistor [tolerance=±5% resistance=1k package=THT]
  LED7 = LED - 3mm [color="Red (633nm)" package="3 mm [THT]"]

nets:
  N1: J1.PC8, J4.pin3
  N2: J1.PC6, J4.pin2
  N3: J1.PC5, J4.pin1
  N4: J1.PB12, J3.pin3
  N5: J1.PC11, J5.pin5
  N6: J1.PD2, J5.pin4
  N7: J1.RESET, J5.pin1
  N8: J1.3v3, J7.pin1
  N9: J1.GND#339, J6.pin1
  N10: J1.D9_PWM, J10.PB1
  N11: J1.D10_PWM/SS, J10.PB12
  N12: J1.D11_PWM/MOSI, J10.PB15
  N13: J1.D12/MISO, J10.PB14
  N14: J1.D13/SCK, J10.PB13
  N15: J1.GND#1157, J10.GND, R1.Pin_0, R2.Pin_0, R3.Pin_0, R4.Pin_0, R5.Pin_0, R6.Pin_0
  N16: J1.PB2, J3.pin2
  N17: J1.PB1, J3.pin1
  N18: J1.PB15, J3.pin7
  N19: J1.PB13, J3.pin8
  N20: J1.PC9, J4.pin4
  N21: J1.PB8, J4.pin5
  N22: J1.PB9, J4.pin6
  N23: J1.PB4, J2.pin1
  N24: J1.PB5, J2.pin2
  N25: J1.PB3, J2.pin3
  N26: J1.PA10, J2.pin4
  N27: J1.PA0, J8.pin1
  N28: J1.PA1, J8.pin2
  N29: J1.PA4, J8.pin3
  N30: J1.PB0, J8.pin4
  N31: J1.PC1, J8.pin5
  N32: J1.PC0, J8.pin6
  N33: J1.PC10, J5.pin3
  N34: J1.PC12, J5.pin2
  N35: J1.PC2, J8.pin7
  N36: J1.PC3, J8.pin8
  N37: J3.pin4, J7.pin3
  N38: J3.pin5, J6.pin2
  N39: J3.pin6, J7.pin2
  N40: J6.pin5, J9.pin1
  N41: J7.pin5, J9.pin2
  N42: J10.D2, LED1.anode
  N43: J10.D3_PWM, LED2.anode
  N44: J10.D4, LED3.anode
  N45: J10.D5_PWM, LED4.anode, LED5.anode
  N46: J10.D6_PWM, LED7.anode
  N47: J10.D7, LED6.anode
  N48: LED1.cathode, R1.Pin_1
  N49: LED2.cathode, R2.Pin_1
  N50: LED3.cathode, R3.Pin_1
  N51: LED4.cathode, LED5.cathode, R4.Pin_1
  N52: LED6.cathode, R6.Pin_1
  N53: R5.Pin_1, LED7.cathode

notes:
  Sequencer UI
  Sequencer UI 2
  POT Controller
  Nucleo Sequencer
  (SPI Slave)
  UI Controller
  (SPI Master)
