# Fritzing sketch LT1054+LinierRegurator (saved by Fritzing 0.9.3b)
breadboards: 1

parts:
  U1 = Voltage Regulator - 5V [package="TO220 [THT]"]
  C1 = Ceramic Capacitor [capacitance=100nF package="100 mil [THT, multilayer]"]
  C2 = Ceramic Capacitor [capacitance=100nF package="100 mil [THT, multilayer]"]
  C3 = Electrolytic Capacitor [capacitance=1µF package="100 mil [THT, electrolytic]"]
  D1 = Rectifier Diode [part_number=1N4001 package="300 mil [THT]"]
  C4 = Electrolytic Capacitor [capacitance=1µF package="100 mil [THT, electrolytic]"]
  IC1 = IC, DIP package, 8 pins [chip_label=LT1054]
  C5 = Electrolytic Capacitor [capacitance=1µF package="100 mil [THT, electrolytic]"]
  C6 = Electrolytic Capacitor [capacitance=1µF package="100 mil [THT, electrolytic]"]
  R1 = Resistor [tolerance=±5% resistance=100 package=THT]
  R2 = Resistor [tolerance=±5% resistance=100 package=THT]
  R3 = Resistor [tolerance=±5% resistance=100 package=THT]
  R4 = Resistor [tolerance=±5% resistance=100 package=THT]
  C7 = Electrolytic Capacitor [capacitance=1µF package="100 mil [THT, electrolytic]"]

nets:
  N1: U1.input_voltage, C1.1, C3.+, D1.cathode
  N2: U1.GND, C1.0, C2.0, C3.-, C4.-, IC1.pin3, C6.-, R1.Pin_1, R2.Pin_1, R3.Pin_1, R4.Pin_1, C7.+
  N3: U1.output_voltage, C2.1, D1.anode, C4.+, IC1.pin8, C6.+, R2.Pin_0, R3.Pin_0, R4.Pin_0
  N4: IC1.pin2, C5.+
  N5: IC1.pin4, C5.-
  N6: IC1.pin5, R1.Pin_0
  N7: IC1.pin6, C7.-

notes:
  GND+12V
  GND
  +9V
  -9V
