# Fritzing sketch TC74HC541HC_SPI_Buffer (saved by Fritzing 0.9.2b)
breadboards: 1

parts:
  IC1 = IC, DIP package, 20 pins [chip_label=TC74HC541AP]
  C1 = Ceramic Capacitor [capacitance=100nF package="100 mil [THT, multilayer]"]
  R1 = Resistor [tolerance=±5% resistance=33 package=THT]
  R2 = Resistor [tolerance=±5% resistance=33 package=THT]

nets:
  N1: IC1.pin1, IC1.pin9, IC1.pin10, IC1.pin19, C1.0
  N2: IC1.pin16, R2.Pin_0
  N3: IC1.pin17, R1.Pin_0
  N4: IC1.pin20, C1.1

notes:
  IN
  SCK
  NC
  MOSI
  CS(DCO)
  CS(DCF)
  CS(DCA)
  LDAC(DCA)
  GND
  GND
  +3.3V
  OUT
  SCK
  NC
  MOSI
  CS(DCO)
  CS(DCF)
  CS(DCA)
  LDAC(DCA)
  GND
