# Fritzing sketch Base Machine Battery (saved by Fritzing 0.9.2b)

parts:
  S1 = Toggle Switch [package=THT]
  S2 = Toggle Switch [package=THT]
  VCC1 = Battery block 9V
  VCC2 = Battery block 9V
  J1 = female pin header, 4 pins [form="♀ (female)"]

nets:
  N1: S1.COM, J1.pin1
  N2: S1.L2, VCC2.+
  N3: S2.COM, J1.pin4
  N4: S2.L2, VCC1.-
  N5: VCC1.+, J1.pin3
  N6: VCC2.-, J1.pin2

notes:
  DPDT SW
