# Fritzing sketch BaseMachine Sequencer (Slave) only (saved by Fritzing 0.9.2b)
perfboards: 3
breadboards: 1

parts:
  J1 = STM32 Nucleo boards
  J10 = female pin header, 5 pins [form="♀ (female)"]
  J11 = female pin header, 4 pins [form="♀ (female)"]  # not connected
  J12 = female pin header, 4 pins [form="♀ (female)"]
  JP1 = RCA [package=rca_lock]  # not connected
  JP2 = RCA [package=rca_lock]  # not connected
  J13 = female pin header, 3 pins [form="♀ (female)"]
  JP3 = RCA [package=rca_lock]  # not connected
  JP4 = RCA [package=rca_lock]  # not connected
  J15 = female pin header, 8 pins [form="♀ (female)"]
  J16 = female pin header, 8 pins [form="♀ (female)"]  # not connected
  J20 = female pin header, 4 pins [form="♀ (female)"]
  JP5 = RCA [package=rca_lock]  # not connected
  J14 = female alternating pin header, 6 pins [form="♀ (female)"]  # not connected
  J17 = female pin header, 8 pins [form="♀ (female)"]
  J21 = female pin header, 2 pins [form="♀ (female)"]
  J22 = female pin header, 2 pins [form="♀ (female)"]  # not connected
  J24 = female pin header, 4 pins [form="♀ (female)"]
  J25 = female pin header, 4 pins [form="♀ (female)"]  # not connected
  J26 = female pin header, 4 pins [form="♀ (female)"]  # not connected
  J27 = female pin header, 4 pins [form="♀ (female)"]  # not connected
  J28 = female pin header, 3 pins [form="♀ (female)"]  # not connected
  J29 = female pin header, 6 pins [form="♀ (female)"]
  R1 = Resistor [tolerance=±5% resistance=33 package=THT]
  LED1 = LED - 3mm [color="Red (633nm)" package="3 mm [THT]"]
  LED2 = LED - 3mm [color="Red (633nm)" package="3 mm [THT]"]
  LED3 = LED - 3mm [color="Red (633nm)" package="3 mm [THT]"]
  LED4 = LED - 3mm [color="Red (633nm)" package="3 mm [THT]"]
  LED5 = LED - 3mm [color="Red (633nm)" package="3 mm [THT]"]
  LED6 = LED - 3mm [color="Red (633nm)" package="3 mm [THT]"]
  LED7 = LED - 3mm [color="Red (633nm)" package="3 mm [THT]"]
  LED8 = LED - 3mm [color="Red (633nm)" package="3 mm [THT]"]
  R2 = Resistor [tolerance=±5% resistance=1k package=THT]
  R3 = Resistor [tolerance=±5% resistance=1k package=THT]
  R4 = Resistor [tolerance=±5% resistance=1k package=THT]
  R5 = Resistor [tolerance=±5% resistance=1k package=THT]
  R6 = Resistor [tolerance=±5% resistance=1k package=THT]
  R7 = Resistor [tolerance=±5% resistance=1k package=THT]
  R8 = Resistor [tolerance=±5% resistance=1k package=THT]
  R9 = Resistor [tolerance=±5% resistance=1k package=THT]

nets:
  N1: J1.A0, LED1.anode
  N2: J1.A1, LED2.anode
  N3: J1.A2, LED3.anode
  N4: J1.A3, LED4.anode
  N5: J1.A4/SDA, LED5.anode
  N6: J1.A5/SCL, LED6.anode
  N7: J1.PB12, J29.pin5
  N8: J1.GND#1157, J29.pin6
  N9: J1.D2, LED7.anode
  N10: J1.D3_PWM, LED8.anode
  N11: J1.3V3, J21.pin2
  N12: J1.5V, J15.pin4
  N13: J1.GND#1188, J15.pin3
  N14: J1.GND#1189, J21.pin1
  N15: J1.PB1, R1.Pin_1
  N16: J1.PB15, J29.pin3
  N17: J1.PB14, J29.pin2
  N18: J1.PB13, J29.pin1
  N19: J1.GND#2223, J10.pin4
  N20: J1.PA5, J10.pin2
  N21: J1.PA7, J10.pin3
  N22: J1.PB6, J17.pin3
  N23: J1.PC7, J24.pin4
  N24: J1.PA9, J10.pin1
  N25: J1.PA8, J10.pin5
  N26: J12.pin1, J20.pin1
  N27: J12.pin2, J20.pin2
  N28: J12.pin3, J20.pin3
  N29: J12.pin4, J20.pin4
  N30: J13.pin1, J17.pin6, J24.pin3
  N31: J13.pin2, J17.pin4, J24.pin2
  N32: J13.pin3, J17.pin7, J24.pin1
  N33: LED1.cathode, R5.Pin_0
  N34: LED2.cathode, R4.Pin_0
  N35: LED3.cathode, R2.Pin_0
  N36: LED4.cathode, R3.Pin_0
  N37: LED5.cathode, R6.Pin_0
  N38: LED6.cathode, R7.Pin_0
  N39: LED7.cathode, R8.Pin_0
  N40: LED8.cathode, R9.Pin_0
  N41: R2.Pin_1, R3.Pin_1, R4.Pin_1, R5.Pin_1, R6.Pin_1, R7.Pin_1, R8.Pin_1, R9.Pin_1

notes:
  PWR OUT
  +9V
  +3.3V
  GND
  -9V
  SPI
  CS
  SCK
  MOSI
  GND
  LDAC
  NJM13700 DCA
  VCVS DCF
  PSoC 4 Prototyping Kit DCO
  IN
  OUT
  +9V -9V
  Battery
  PWR
  GND
  3.3V
  SPI
  GND
  MOSI
  SCK
  CS
  SPI (to Master)
  SCK
  MISO
  MOSI
  Interrupt
  CS
  GND
