# Fritzing sketch BaseMachine Sequencer 統合版 (saved by Fritzing 0.9.3b)
perfboards: 3

parts:
  J10 = female pin header, 5 pins [form="♀ (female)"]  # not connected
  J11 = female pin header, 4 pins [form="♀ (female)"]  # not connected
  J12 = female pin header, 4 pins [form="♀ (female)"]
  JP1 = RCA [package=rca_lock]  # not connected
  JP2 = RCA [package=rca_lock]  # not connected
  J13 = female pin header, 3 pins [form="♀ (female)"]
  JP3 = RCA [package=rca_lock]  # not connected
  JP4 = RCA [package=rca_lock]  # not connected
  J15 = female pin header, 8 pins [form="♀ (female)"]  # not connected
  J16 = female pin header, 8 pins [form="♀ (female)"]  # not connected
  J20 = female pin header, 4 pins [form="♀ (female)"]
  JP5 = RCA [package=rca_lock]  # not connected
  J14 = female alternating pin header, 6 pins [form="♀ (female)"]  # not connected
  J17 = female pin header, 8 pins [form="♀ (female)"]
  J21 = female pin header, 2 pins [form="♀ (female)"]  # not connected
  J22 = female pin header, 2 pins [form="♀ (female)"]  # not connected
  J24 = female pin header, 4 pins [form="♀ (female)"]
  J25 = female pin header, 4 pins [form="♀ (female)"]  # not connected
  J26 = female pin header, 4 pins [form="♀ (female)"]  # not connected
  J27 = female pin header, 4 pins [form="♀ (female)"]  # not connected
  J28 = female pin header, 3 pins [form="♀ (female)"]  # not connected

nets:
  N1: J12.pin1, J20.pin1
  N2: J12.pin2, J20.pin2
  N3: J12.pin3, J20.pin3
  N4: J12.pin4, J20.pin4
  N5: J13.pin1, J17.pin6, J24.pin3
  N6: J13.pin2, J17.pin4, J24.pin2
  N7: J13.pin3, J17.pin7, J24.pin1

notes:
  PWR OUT
  +9V
  +3.3V
  GND
  -9V
  SPI
  CS
  SCK
  MOSI
  GND
  LDAC
  NJM13700 DCA
  VCVS DCF
  PSoC 4 Prototyping Kit DCO
  IN
  OUT
  +9V -9V
  Battery
  PWR
  GND
  3.3V
  SPI
  GND
  MOSI
  SCK
  CS
