# Fritzing sketch BaseMachine Synth Board (saved by Fritzing 0.9.2b)
perfboards: 3

parts:
  J1 = STM32 Nucleo boards
  J10 = female pin header, 5 pins [form="♀ (female)"]
  J11 = female pin header, 4 pins [form="♀ (female)"]
  J12 = female pin header, 4 pins [form="♀ (female)"]
  JP1 = RCA [package=rca_lock]  # not connected
  JP2 = RCA [package=rca_lock]  # not connected
  J13 = female pin header, 3 pins [form="♀ (female)"]
  JP3 = RCA [package=rca_lock]  # not connected
  JP4 = RCA [package=rca_lock]  # not connected
  J15 = female pin header, 8 pins [form="♀ (female)"]
  J16 = female pin header, 8 pins [form="♀ (female)"]  # not connected
  J20 = female pin header, 4 pins [form="♀ (female)"]
  JP5 = RCA [package=rca_lock]  # not connected
  J14 = female alternating pin header, 6 pins [form="♀ (female)"]  # not connected
  J17 = female pin header, 8 pins [form="♀ (female)"]
  J21 = female pin header, 2 pins [form="♀ (female)"]
  J22 = female pin header, 2 pins [form="♀ (female)"]  # not connected
  J24 = female pin header, 4 pins [form="♀ (female)"]
  J25 = female pin header, 4 pins [form="♀ (female)"]  # not connected
  J26 = female pin header, 4 pins [form="♀ (female)"]
  J27 = female pin header, 4 pins [form="♀ (female)"]  # not connected
  J28 = female pin header, 3 pins [form="♀ (female)"]  # not connected

nets:
  N1: J1.GND, J10.pin4
  N2: J1.PA5, J10.pin2
  N3: J1.PA7, J10.pin3
  N4: J1.PB6, J17.pin3
  N5: J1.PC7, J24.pin4
  N6: J1.PA9, J10.pin1
  N7: J1.PA8, J10.pin5
  N8: J11.pin2, J15.pin5
  N9: J11.pin3, J15.pin3
  N10: J12.pin1, J20.pin1
  N11: J12.pin2, J20.pin2
  N12: J12.pin3, J20.pin3
  N13: J12.pin4, J20.pin4
  N14: J13.pin1, J17.pin6, J24.pin3
  N15: J13.pin2, J17.pin4, J24.pin2
  N16: J13.pin3, J17.pin7, J24.pin1
  N17: J21.pin1, J26.pin3
  N18: J21.pin2, J26.pin2

notes:
  PWR OUT
  +9V
  +3.3V
  GND
  -9V
  SPI
  CS
  SCK
  MOSI
  GND
  LDAC
  NJM13700 DCA
  VCVS DCF
  PSoC 4 Prototyping Kit DCO
  IN
  OUT
  +9V -9V
  Battery
  PWR
  GND
  3.3V
  SPI
  GND
  MOSI
  SCK
  CS
