# Fritzing sketch BaseMachine UI Controller (Master) only (saved by Fritzing 0.9.2b)
perfboards: 3

parts:
  J1 = STM32 Nucleo boards
  J3 = female pin header, 8 pins [form="♀ (female)"]
  J4 = female pin header, 6 pins [form="♀ (female)"]
  J2 = female pin header, 6 pins [form="♀ (female)"]
  J5 = female pin header, 5 pins [form="♀ (female)"]
  J6 = female pin header, 5 pins [form="♀ (female)"]
  J7 = female pin header, 5 pins [form="♀ (female)"]
  J8 = female pin header, 8 pins [form="♀ (female)"]
  J9 = female pin header, 2 pins [form="♀ (female)"]
  U1 = mystery part, 8 pins [chip_label="4x4 keypad"]
  J10 = female pin header, 7 pins [form="♀ (female)"]

nets:
  N1: J1.PC8, J4.pin3
  N2: J1.PC6, J4.pin2
  N3: J1.PC5, J4.pin1
  N4: J1.PA12, J4.pin5
  N5: J1.PA11, J4.pin6
  N6: J1.PB12, J3.pin3
  N7: J1.PC11, J5.pin5
  N8: J1.PD2, J5.pin4
  N9: J1.RESET, J5.pin1
  N10: J1.3v3, J7.pin1
  N11: J1.GND#339, J6.pin1
  N12: J1.D9_PWM, J10.pin1
  N13: J1.D10_PWM/SS, J10.pin2
  N14: J1.D11_PWM/MOSI, J10.pin3
  N15: J1.D12/MISO, J10.pin4
  N16: J1.D13/SCK, J10.pin5
  N17: J1.GND#1157, J10.pin6
  N18: J1.AREF, J10.pin7
  N19: J1.PB2, J3.pin2
  N20: J1.PB1, J3.pin1
  N21: J1.PB15, J3.pin7
  N22: J1.PB13, J3.pin8
  N23: J1.PC9, J4.pin4
  N24: J1.PA9, U1.pin6
  N25: J1.PA8, U1.pin7
  N26: J1.PB10, U1.pin8
  N27: J1.PB4, J2.pin1
  N28: J1.PB5, J2.pin2
  N29: J1.PB3, J2.pin3
  N30: J1.PA10, J2.pin4
  N31: J1.PA0, J8.pin8
  N32: J1.PA1, J8.pin7
  N33: J1.PA4, J8.pin6
  N34: J1.PB0, J8.pin5
  N35: J1.PC1, J8.pin4
  N36: J1.PC0, J8.pin3
  N37: J1.PC10, J5.pin3
  N38: J1.PC12, J5.pin2
  N39: J1.PA13, U1.pin1
  N40: J1.PA14, U1.pin2
  N41: J1.PA15, U1.pin3
  N42: J1.PB7, U1.pin4
  N43: J1.PC13, U1.pin5
  N44: J1.PC2, J8.pin2
  N45: J1.PC3, J8.pin1
  N46: J3.pin4, J7.pin2
  N47: J3.pin5, J6.pin3
  N48: J3.pin6, J7.pin3
  N49: J6.pin5, J9.pin2
  N50: J7.pin5, J9.pin1

notes:
  Sequencer UI
  Sequencer UI 2
  POT Controller
  UI Controller
  (SPI Master)
  SPI (to Slave)
  Interrupt
  CS
  MOSI
  MISO
  SCK
  GND
  RESET
