# Fritzing sketch BaseMachine統合版2 (saved by Fritzing 0.9.3b)
perfboards: 8
breadboards: 2

parts:
  J1 = STM32 Nucleo boards
  J3 = female pin header, 8 pins [form="♀ (female)"]
  J4 = female pin header, 6 pins [form="♀ (female)"]
  J2 = female pin header, 6 pins [form="♀ (female)"]
  J5 = female pin header, 5 pins [form="♀ (female)"]
  J6 = female pin header, 5 pins [form="♀ (female)"]
  J7 = female pin header, 5 pins [form="♀ (female)"]
  J8 = female pin header, 8 pins [form="♀ (female)"]
  J9 = female pin header, 2 pins [form="♀ (female)"]
  J29 = female pin header, 2 pins [form="♀ (female)"]  # not connected
  J30 = female pin header, 2 pins [form="♀ (female)"]
  J33 = female pin header, 5 pins [form="♀ (female)"]  # not connected
  J34 = female pin header, 4 pins [form="♀ (female)"]  # not connected
  J35 = female pin header, 4 pins [form="♀ (female)"]  # not connected
  J36 = female pin header, 4 pins [form="♀ (female)"]  # not connected
  J37 = female pin header, 4 pins [form="♀ (female)"]
  JP6 = RCA [package=rca_lock]  # not connected
  JP7 = RCA [package=rca_lock]  # not connected
  JP8 = RCA [package=rca_lock]  # not connected
  JP9 = RCA [package=rca_lock]  # not connected
  JP10 = RCA [package=rca_lock]  # not connected
  J38 = female pin header, 3 pins [form="♀ (female)"]  # not connected
  J39 = female pin header, 3 pins [form="♀ (female)"]  # not connected
  J40 = female alternating pin header, 6 pins [form="♀ (female)"]  # not connected
  J41 = female pin header, 8 pins [form="♀ (female)"]
  J42 = female pin header, 8 pins [form="♀ (female)"]  # not connected
  J43 = female pin header, 8 pins [form="♀ (female)"]  # not connected
  J44 = female pin header, 4 pins [form="♀ (female)"]
  IC2 = IC, DIP package, 28 pins [chip_label=MCP23S17]
  C3 = Ceramic Capacitor [capacitance=100nF package="100 mil [THT, multilayer]"]
  C4 = Electrolytic Capacitor [capacitance=1µF package="100 mil [THT, electrolytic]"]
  R5 = Resistor [tolerance=±5% resistance=3.3k package=THT]
  IC3 = IC, DIP package, 20 pins [chip_label=74HC541]  # not connected
  J31 = female pin header, 5 pins [form="♀ (female)"]  # not connected

nets:
  N1: J1.PC8, J4.pin3
  N2: J1.PC6, J4.pin2
  N3: J1.PC5, J4.pin1
  N4: J1.PA12, J4.pin5
  N5: J1.PA11, J4.pin6
  N6: J1.PB12, J3.pin3
  N7: J1.PC11, IC2.pin14, R5.Pin_0
  N8: J1.PD2, IC2.pin11
  N9: J1.GND#333, IC2.pin9, C3.0, C4.+
  N10: J1.RESET, J5.pin1
  N11: J1.3v3, J7.pin1
  N12: J1.GND#339, J6.pin1
  N13: J1.3V3, J30.pin2
  N14: J1.5V, J41.pin4
  N15: J1.GND#1188, J30.pin1
  N16: J1.GND#1189, J41.pin2
  N17: J1.PB2, J3.pin2
  N18: J1.PB1, J3.pin1
  N19: J1.PB15, J3.pin7
  N20: J1.PB13, J3.pin8
  N21: J1.PC9, J4.pin4
  N22: J1.PB4, J2.pin1
  N23: J1.PB5, J2.pin2
  N24: J1.PB3, J2.pin3
  N25: J1.PA10, J2.pin4
  N26: J1.PA0, J8.pin8
  N27: J1.PA1, J8.pin7
  N28: J1.PA4, J8.pin6
  N29: J1.PB0, J8.pin5
  N30: J1.PC1, J8.pin4
  N31: J1.PC0, J8.pin3
  N32: J1.PC10, IC2.pin12
  N33: J1.PC12, IC2.pin13
  N34: J1.VDD, IC2.pin10, IC2.pin15, IC2.pin16, IC2.pin17, C3.1, C4.-, R5.Pin_1
  N35: J1.PA13, IC2.pin18
  N36: J1.PA15, J5.pin2
  N37: J1.GND#3328, J5.pin3
  N38: J1.PB7, J5.pin4
  N39: J1.PC13, J5.pin5
  N40: J1.PC2, J8.pin2
  N41: J1.PC3, J8.pin1
  N42: J3.pin4, J7.pin2
  N43: J3.pin5, J6.pin3
  N44: J3.pin6, J7.pin3
  N45: J6.pin5, J9.pin2
  N46: J7.pin5, J9.pin1
  N47: J37.pin1, J44.pin1
  N48: J37.pin2, J44.pin2
  N49: J37.pin3, J44.pin3
  N50: J37.pin4, J44.pin4

notes:
  Sequencer UI
  Sequencer UI 2
  POT Controller
  PWR
  GND
  3.3V
  RESET
  GND
  MOSI
  SCK
  CS
  PWR OUT
  +9V
  +3.3V
  GND
  -9V
  SPI
  CS
  SCK
  MOSI
  GND
  LDAC
  NJM13700 DCA
  VCVS DCF
  PSoC 4 Prototyping Kit DCO
  IN
  OUT
  +9V -9V
  Battery
  MCP23S17
  1 GPB0 28 GPA7
  2 GPB1 27 GPA6
  3 GPB2 26 GPA5
  4 GPB3 25 GPA4
  5 GPB4 24 GPA3
  6 GPB5 23 GPA2
  7 GPB6 22 GPA1
  8 GPB7 21 GPA0
  9 VDD 20 INTA
  10 VSS 19 INTB
  11 !CS 18 !RESET
  12 SCK 17 A2
  13 SI 16 A1
  14 SO 15 A0
  Switchx8
  GND
  +3.3V
  GND
  +5V
  GND
  SCK
  MOSI
  CS(DCO)
  CS(DCF)
  CS(DCA)
  LDAC(DCA)
