# Fritzing sketch Nucleo Sequencer & PSoC4 DCO (saved by Fritzing 0.9.2b)
breadboards: 3
perfboards: 1

parts:
  J1 = STM32 Nucleo boards
  S1 = Pushbutton [package="[THT]"]
  S2 = Pushbutton [package="[THT]"]
  S3 = Pushbutton [package="[THT]"]
  S4 = Pushbutton [package="[THT]"]
  S5 = Pushbutton [package="[THT]"]
  U1 = mystery part, 8 pins [chip_label=Nokia5110]
  R1 = Rotary Potentiometer (Small) [maximum_resistance=100kΩ package=THT]
  R2 = Rotary Potentiometer (Small) [maximum_resistance=100kΩ package=THT]
  R3 = Rotary Potentiometer (Small) [maximum_resistance=100kΩ package=THT]
  U2 = JOYSTICK-PSP1000 [package=joystick-psp1000]
  S6 = Pushbutton [package="[THT]"]
  S7 = Pushbutton [package="[THT]"]
  RE1 = Rotary Encoder [package=THT]
  RE2 = Rotary Encoder [package=THT]
  J2 = female pin header, 9 pins [form="♀ (female)"]
  J3 = female pin header, 9 pins [form="♀ (female)"]
  J4 = female pin header, 8 pins [form="♀ (female)"]  # not connected
  J5 = female pin header, 8 pins [form="♀ (female)"]
  J6 = female pin header, 10 pins [form="♀ (female)"]
  J7 = female pin header, 6 pins [form="♀ (female)"]
  J8 = female pin header, 6 pins [form="♀ (female)"]
  R4 = Resistor [tolerance=±5% resistance=1k package=THT]

nets:
  N1: J1.A0, R3.wiper
  N2: J1.A1, R2.wiper
  N3: J1.A2, R1.wiper
  N4: J1.A3, U2.X
  N5: J1.A4/SDA, U2.Y
  N6: J1.PA11, U1.pin8
  N7: J1.PB12, U1.pin5
  N8: J1.D10_PWM/SS, J5.pin3
  N9: J1.D11_PWM/MOSI, J5.pin1
  N10: J1.D12/MISO, J5.pin2
  N11: J1.D13/SCK, J6.pin6
  N12: J1.GND#1157, J6.pin7, R4.Pin_0
  N13: J1.D2, RE1.EncoderPinA
  N14: J1.D3_PWM, RE1.EncoderPinB
  N15: J1.D4, RE2.EncoderPinA
  N16: J1.D5_PWM, RE2.EncoderPinB
  N17: J1.D6_PWM, S6.Pin_1, S6.Pin_2
  N18: J1.D7, S7.Pin_1, S7.Pin_2
  3V3: J1.3V3, U1.pin1, R1.leg2, R2.leg2, R3.leg2, U2.VCC
  N19: J1.GND#1188, S1.Pin_1, S1.Pin_2, S2.Pin_1, S2.Pin_2, S3.Pin_1, S3.Pin_2, S4.Pin_1, S4.Pin_2, S5.Pin_1, S5.Pin_2, U1.pin2, R1.leg1, R2.leg1, R3.leg1, U2.GND, S6.Pin_3, S6.Pin_4, S7.Pin_4, RE1.EncoderPinC, RE2.EncoderPinC
  N20: J1.PB2, U1.pin4
  N21: J1.PB1, U1.pin3
  N22: J1.PB15, U1.pin6
  N23: J1.PB13, U1.pin7
  N24: J1.PA13, S1.Pin_3, S1.Pin_4
  N25: J1.PA14, S2.Pin_3, S2.Pin_4
  N26: J1.PA15, S3.Pin_3, S3.Pin_4
  N27: J1.PB7, S4.Pin_3, S4.Pin_4
  N28: J1.PC13, S5.Pin_3, S5.Pin_4
  N29: J2.pin1, J3.pin1, R4.Pin_1
  N30: J6.pin9, J7.pin2
  N31: J6.pin10, J8.pin2

notes:
  PSoC 4 Pioneer Kit
  WaveOut
  Check1/2
