# Fritzing sketch NucleoF401RE シーケンサー&PSoC4 DCO (saved by Fritzing 0.9.2b)
breadboards: 2
perfboards: 1

parts:
  J1 = female pin header, 9 pins [form="♀ (female)"]
  J2 = female pin header, 8 pins [form="♀ (female)"]
  J3 = female pin header, 9 pins [form="♀ (female)"]
  J4 = female pin header, 8 pins [form="♀ (female)"]
  J5 = female pin header, 10 pins [form="♀ (female)"]
  J6 = female pin header, 6 pins [form="♀ (female)"]
  J7 = female pin header, 6 pins [form="♀ (female)"]
  LCD1 = LCD screen
  R1 = Resistor [tolerance=±5% resistance=220 package=THT]
  R2 = TRIMPOT [package=3362u-2]
  R3 = Resistor [tolerance=±5% resistance=1k package=THT]
  J8 = STM32 Nucleo boards

nets:
  N1: J1.pin1, J3.pin1, R3.Pin_0
  N2: J1.pin4, LCD1.RS
  N3: J1.pin5, LCD1.E
  N4: J1.pin6, LCD1.DB7
  N5: J1.pin7, LCD1.DB6
  N6: J1.pin8, LCD1.DB5
  N7: J1.pin9, LCD1.DB4
  N8: J2.pin3, LCD1.VSS, LCD1.LED-, R2.CCW, R3.Pin_1
  N9: J2.pin4, LCD1.VDD, R1.Pin_1, R2.CW
  N10: J4.pin1, J8.D11_PWM/MOSI
  N11: J4.pin2, J8.D12/MISO
  N12: J4.pin3, J8.D10_PWM/SS
  N13: J5.pin1, LCD1.R/W
  N14: J5.pin6, J8.D13/SCK
  N15: J5.pin7, J8.GND
  N16: J5.pin9, J7.pin2
  N17: J5.pin10, J6.pin2
  N18: LCD1.V0, R2.WIPER
  N19: LCD1.LED+, R1.Pin_0

notes:
  PSoC4 Pioneer Kit
  WaveOut
