# Fritzing sketch Sequencer UI board 2 (saved by Fritzing 0.9.2b)
perfboards: 3

parts:
  J1 = STM32 Nucleo boards
  J3 = female pin header, 8 pins [form="♀ (female)"]
  J4 = female pin header, 6 pins [form="♀ (female)"]
  J2 = female pin header, 6 pins [form="♀ (female)"]
  J5 = female pin header, 5 pins [form="♀ (female)"]
  J6 = female pin header, 5 pins [form="♀ (female)"]
  J7 = female pin header, 5 pins [form="♀ (female)"]
  J8 = female pin header, 8 pins [form="♀ (female)"]
  J9 = female pin header, 2 pins [form="♀ (female)"]

nets:
  N1: J1.PC8, J4.pin3
  N2: J1.PC6, J4.pin2
  N3: J1.PC5, J4.pin1
  N4: J1.PB12, J3.pin3
  N5: J1.PC11, J5.pin5
  N6: J1.PD2, J5.pin4
  N7: J1.RESET, J5.pin1
  N8: J1.3v3, J7.pin1
  N9: J1.GND, J6.pin1
  N10: J1.PB2, J3.pin2
  N11: J1.PB1, J3.pin1
  N12: J1.PB15, J3.pin7
  N13: J1.PB13, J3.pin8
  N14: J1.PC9, J4.pin4
  N15: J1.PB8, J4.pin5
  N16: J1.PB9, J4.pin6
  N17: J1.PB4, J2.pin1
  N18: J1.PB5, J2.pin2
  N19: J1.PB3, J2.pin3
  N20: J1.PA10, J2.pin4
  N21: J1.PA0, J8.pin1
  N22: J1.PA1, J8.pin2
  N23: J1.PA4, J8.pin3
  N24: J1.PB0, J8.pin4
  N25: J1.PC1, J8.pin5
  N26: J1.PC0, J8.pin6
  N27: J1.PC10, J5.pin3
  N28: J1.PC12, J5.pin2
  N29: J1.PC2, J8.pin7
  N30: J1.PC3, J8.pin8
  N31: J3.pin4, J7.pin3
  N32: J3.pin5, J6.pin2
  N33: J3.pin6, J7.pin2
  N34: J6.pin5, J9.pin1
  N35: J7.pin5, J9.pin2

notes:
  Sequencer UI
  Sequencer UI 2
  POT Controller
