# Fritzing sketch Sequencer UI board 3 (saved by Fritzing 0.9.2b)
perfboards: 6

parts:
  J1 = STM32 Nucleo boards
  J3 = female pin header, 8 pins [form="♀ (female)"]
  J4 = female pin header, 6 pins [form="♀ (female)"]
  J2 = female pin header, 6 pins [form="♀ (female)"]
  J5 = female pin header, 5 pins [form="♀ (female)"]
  J6 = female pin header, 5 pins [form="♀ (female)"]
  J7 = female pin header, 5 pins [form="♀ (female)"]
  J8 = female pin header, 8 pins [form="♀ (female)"]
  J9 = female pin header, 2 pins [form="♀ (female)"]
  J10 = female pin header, 5 pins [form="♀ (female)"]
  J11 = female pin header, 4 pins [form="♀ (female)"]
  J12 = female pin header, 4 pins [form="♀ (female)"]
  JP1 = RCA [package=rca_lock]
  JP2 = RCA [package=rca_lock]  # not connected
  J13 = female pin header, 3 pins [form="♀ (female)"]
  JP3 = RCA [package=rca_lock]
  JP4 = RCA [package=rca_lock]
  J14 = female pin header, 10 pins [form="♀ (female)"]
  J15 = female pin header, 8 pins [form="♀ (female)"]
  J16 = female pin header, 8 pins [form="♀ (female)"]
  J17 = female pin header, 9 pins [form="♀ (female)"]  # not connected
  J18 = female pin header, 9 pins [form="♀ (female)"]  # not connected
  J19 = female pin header, 2 pins [form="♀ (female)"]
  J20 = female pin header, 4 pins [form="♀ (female)"]

nets:
  N1: J1.PC8, J4.pin3
  N2: J1.PC6, J4.pin2
  N3: J1.PC5, J4.pin1
  N4: J1.PA11, J3.pin4
  N5: J1.PB12, J3.pin3
  N6: J1.PC11, J5.pin5
  N7: J1.PD2, J5.pin4
  N8: J1.RESET, J5.pin1
  N9: J1.3v3, J7.pin1
  N10: J1.GND#339, J6.pin1
  N11: J1.D9_PWM, J15.pin6
  N12: J1.5V, J16.pin8
  N13: J1.GND#1188, J16.pin7
  N14: J1.PB2, J3.pin2
  N15: J1.PB1, J3.pin1
  N16: J1.PB15, J3.pin7
  N17: J1.PB13, J3.pin8
  N18: J1.PC9, J4.pin4
  N19: J1.PB8, J4.pin5
  N20: J1.PB9, J4.pin6
  N21: J1.GND#2223, J10.pin4
  N22: J1.PA5, J10.pin2
  N23: J1.PA7, J10.pin3
  N24: J1.PA9, J10.pin1
  N25: J1.PA8, J10.pin5
  N26: J1.PB4, J2.pin1
  N27: J1.PB5, J2.pin2
  N28: J1.PB3, J2.pin3
  N29: J1.PA10, J2.pin4
  N30: J1.GND#3310, J11.pin3
  N31: J1.VIN, J11.pin1
  N32: J1.PA0, J8.pin1
  N33: J1.PA1, J8.pin2
  N34: J1.PA4, J8.pin3
  N35: J1.PB0, J8.pin4
  N36: J1.PC1, J8.pin5
  N37: J1.PC0, J8.pin6
  N38: J1.PC10, J5.pin3
  N39: J1.PC12, J5.pin2
  N40: J1.PC2, J8.pin7
  N41: J1.PC3, J8.pin8
  N42: J3.pin5, J6.pin2
  N43: J3.pin6, J7.pin2
  N44: J6.pin5, J9.pin1
  N45: J7.pin5, J9.pin2
  N46: J12.pin1, J20.pin1
  N47: J12.pin2, J20.pin2
  N48: J12.pin3, J20.pin3
  N49: J12.pin4, J20.pin4
  N50: JP1.PIN, JP3.PIN
  N51: JP1.SHELL, JP3.SHELL
  N52: J13.pin1, J14.pin5
  N53: J13.pin2, J14.pin7
  N54: JP4.PIN, J19.pin2
  N55: JP4.SHELL, J19.pin1

notes:
  Sequencer UI
  Sequencer UI 2
  POT Controller
  PWR OUT
  +9V
  +3.3V
  GND
  -9V
  SPI
  CS
  SCK
  MOSI
  GND
  LDAC
  NJM13700 DCA
  VCVS DCF
  on Nucleo
  Arduino Header
  PSoC 4 DCO
  IN
  OUT
  +9V -9V
  Battery
