# Fritzing sketch Sequencer UI board (saved by Fritzing 0.9.2b)
perfboards: 1

parts:
  J1 = STM32 Nucleo boards
  J3 = female pin header, 8 pins [form="♀ (female)"]
  J4 = female pin header, 6 pins [form="♀ (female)"]
  J2 = female pin header, 6 pins [form="♀ (female)"]

nets:
  N1: J1.PB12, J3.pin3
  N2: J1.3v3, J3.pin6
  N3: J1.GND, J3.pin5
  N4: J1.PB2, J3.pin2
  N5: J1.PB1, J3.pin1
  N6: J1.PB15, J3.pin7
  N7: J1.PB13, J3.pin8
  N8: J1.PB4, J2.pin1
  N9: J1.PB5, J2.pin2
  N10: J1.PB3, J4.pin5
  N11: J1.PA10, J4.pin6
  N12: J1.PC10, J2.pin3
  N13: J1.PC12, J2.pin4
  N14: J1.VDD, J3.pin4
  N15: J1.PA13, J4.pin1
  N16: J1.PA14, J4.pin2
  N17: J1.PA15, J4.pin3
  N18: J1.PB7, J4.pin4

notes:
  Sequencer UI
