# Fritzing sketch Sequencer UI (saved by Fritzing 0.9.2b)
breadboards: 2

parts:
  U1 = Graphical LCD 128x64 [package=lcd-g12864]  # not connected
  S1 = Pushbutton [package="[THT]"]
  S2 = Pushbutton [package="[THT]"]
  S3 = Pushbutton [package="[THT]"]
  S4 = Pushbutton [package="[THT]"]
  S5 = SWITCH-MOMENTARY-2 [package=tactile-pth-12mm]
  S6 = Pushbutton [package="[THT]"]
  S7 = Pushbutton [package="[THT]"]
  S8 = Pushbutton [package="[THT]"]
  RE1 = Rotary Encoder [package=THT]
  RE3 = Rotary Encoder [package=THT]
  RE2 = Rotary Encoder [package=THT]

nets:
  N1: S1.Pin_1, S1.Pin_2
  N2: S1.Pin_3, S1.Pin_4, S2.Pin_3, S2.Pin_4, S3.Pin_3, S3.Pin_4, S4.Pin_3, S4.Pin_4, S5.1, S6.Pin_3, S6.Pin_4, RE1.EncoderPinC, RE2.EncoderPinC
  N3: S2.Pin_1, S2.Pin_2
  N4: S3.Pin_1, S3.Pin_2
  N5: S4.Pin_1, S4.Pin_2
  N6: S6.Pin_1, S6.Pin_2
  N7: S7.Pin_1, S7.Pin_2
  N8: S7.Pin_3, S7.Pin_4, S8.Pin_3, S8.Pin_4, RE3.EncoderPinC
  N9: S8.Pin_1, S8.Pin_2

notes:
  Octave Up
  Octave Down
  Pitch
  Run
  NoteOn
  Tie
  Accent
  Step
  Mode
  Wave
  Shape
  BPM
